# Fritzing sketch ArduTracker (saved by Fritzing 0.9.3b)

parts:
  microSD1 = MicroSD Card Module  # not connected
  Part1 = NRF24L01  # not connected
  LED1 = LED - 5mm [color="Red (633nm)" package="5 mm [THT]"]
  LED2 = LED - 5mm [color="Red (633nm)" package="5 mm [THT]"]
  U1 = ESP8266 NodeMCU LoLin module  # not connected
  R1 = Resistor [tolerance=±5% resistance=220 package="1206 [SMD]"]
  R2 = Resistor [tolerance=±5% resistance=220 package="1206 [SMD]"]

nets:
  N1: LED1.anode, R2.Pin_0
  N2: LED2.anode, R1.Pin_0

custom parts:
  ESP8266 NodeMCU LoLin module: ESP8266 based NodeMCU
