# Fritzing sketch ArduTracker_esp32 (saved by Fritzing 0.9.4)

parts:
  Micro_SD_Card_Reader = MicroSD Card Module
  nRF24L01 = NRF24L01
  Espressif = ESP-WROOM-32D [part_number=ESP32-WROOM-32D]
  R1 = Resistor [tolerance=±5% resistance=330k package="0805 [SMD]"]

nets:
  GND: Micro_SD_Card_Reader.GND, nRF24L01.MISO, nRF24L01.GND, Espressif.GPIO19, Espressif.GND, R1.Pin_0
  VCC: Micro_SD_Card_Reader.VCC, Espressif.GPIO11, Espressif.VIN
  N1: Micro_SD_Card_Reader.MISO, R1.Pin_1
  N2: Micro_SD_Card_Reader.MOSI, nRF24L01.MOSI, Espressif.GPIO23
  N3: Micro_SD_Card_Reader.SCK, nRF24L01.SCK, Espressif.GPIO18
  N4: Micro_SD_Card_Reader.CS, Espressif.GPIO1, Espressif.GPIO22
  N5: nRF24L01.CSN, Espressif.GPIO17, Espressif.GPIO5
  N6: nRF24L01.VCC, Espressif.3.3, Espressif.EN
  N7: nRF24L01.CE, Espressif.GPIO0, Espressif.GPIO4

notes:
  On the 3.3v SD card cannot be read, use the 5v instaed.
  IMPORTANT: Make sure the red led in the ESP is ON after connecting the power. Otherwise, turn it off immediatly and check the cables or something might start burning.

custom parts:
  ESP-WROOM-32D: HiLetgo ESP-WROOM-32 ESP32 ESP-32S Development Board 2.4GHz Dual-Mode WiFi + Bluetooth Dual Cores Microcontroller The ESP32 integrated with Antenna switches, RF Balun, power amplifiers, low-noise amplifiers, filters, and management modules, and the entire solution occupies the least area of PCB. 2.4 GHz Wi-Fi plus Bluetooth dual-mode chip, with TSMC Ultra-low power consumption 40nm technology,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
